# Fritzing sketch elec (saved by Fritzing 0.8.5b)
circuit board: 3cm x 3cm
breadboards: 1

parts:
  R1 = Resistor [tolerance=±5% resistance=1k package=THT]
  R3 = Resistor [tolerance=±5% resistance=100 package=THT]
  Q1 = NPN-Transistor [package="TO92 [THT]"]
  R4 = Photocell (LDR) [package=THT]
  R5 = Resistor [tolerance=±5% resistance=10k package=THT]
  Raspberry_Pi_B_rev2 = Raspberry Pi B rev2  # not connected
  J1 = Screw terminal - 2 pins [package=THT]  # not connected

nets:
  N1: R1.Pin_0, Q1.C, R5.Pin_0
  N2: R3.Pin_0, Q1.B, R4.pin_0
  N3: R3.Pin_1, Q1.E
  N4: R4.pin_1, R5.Pin_1
